// Logisim project ALU_16bit.circ as structural Verilog: 2 circuits, main circuit ALUUI
module ALUUI (
);

  wire alu_1_ng, alu_1_zr, flags_sw1, flags_sw2, flags_sw3, flags_sw4, flags_sw5, flags_sw6;
  wire [7:0] yl_sw8;
  wire [15:0] alu_1_out_9, xl_sw8;

  DipSwitch xu (
    .sw1(xl_sw8[15]), .sw2(xl_sw8[14]), .sw3(xl_sw8[13]), .sw4(xl_sw8[12]), .sw5(xl_sw8[11]),
    .sw6(xl_sw8[10]), .sw7(xl_sw8[9]), .sw8(xl_sw8[8]));
  DipSwitch xl (
    .sw1(xl_sw8[7]), .sw2(xl_sw8[6]), .sw3(xl_sw8[5]), .sw4(xl_sw8[4]), .sw5(xl_sw8[3]), .sw6(xl_sw8[2]),
    .sw7(xl_sw8[1]), .sw8(xl_sw8[0]));
  DipSwitch yl (
    .sw1(yl_sw8[7]), .sw2(yl_sw8[6]), .sw3(yl_sw8[5]), .sw4(yl_sw8[4]), .sw5(yl_sw8[3]), .sw6(yl_sw8[2]),
    .sw7(yl_sw8[1]), .sw8(yl_sw8[0]));
  DipSwitch flags (
    .sw1(flags_sw1), .sw2(flags_sw2), .sw3(flags_sw3), .sw4(flags_sw4), .sw5(flags_sw5), .sw6(flags_sw6));  // open: sw7, sw8
  ALU alu_1 (
    .x(xl_sw8), .zx(flags_sw1), .nx(flags_sw2), .f(flags_sw3), .y({{8{1'b0}}, yl_sw8}), .zy(flags_sw4),
    .ny(flags_sw5), .no(flags_sw6), .out_9(alu_1_out_9), .zr(alu_1_zr), .ng(alu_1_ng));
  LED zr (.in(alu_1_zr));
  LED ng (.in(alu_1_ng));
  LedBar #(.matrixcols(16)) o (
    .led0(alu_1_out_9[15]), .led1(alu_1_out_9[14]), .led2(alu_1_out_9[13]), .led3(alu_1_out_9[12]),
    .led4(alu_1_out_9[11]), .led5(alu_1_out_9[10]), .led6(alu_1_out_9[9]), .led7(alu_1_out_9[8]),
    .led8(alu_1_out_9[7]), .led9(alu_1_out_9[6]), .led10(alu_1_out_9[5]), .led11(alu_1_out_9[4]),
    .led12(alu_1_out_9[3]), .led13(alu_1_out_9[2]), .led14(alu_1_out_9[1]), .led15(alu_1_out_9[0]));
endmodule

module ALU (
  input  [15:0] x,
  input  zx,
  input  nx,
  input  f,
  input  [15:0] y,
  input  zy,
  input  ny,
  input  no,
  output [15:0] out_9,
  output zr,
  output ng
);

  wire or_1_out;
  wire [15:0] add16_1_p2, and_1_out, multiplexer_1_out, multiplexer_2_out, multiplexer_3_out,
       multiplexer_4_out, multiplexer_6_out, not_1_out, not_2_out, not_3_out;

  Multiplexer #(.width(16)) multiplexer_1 (.in0(x), .in1({16{1'b0}}), .out(multiplexer_1_out), .sel(zx));
  Multiplexer #(.width(16)) multiplexer_2 (.in0(y), .in1({16{1'b0}}), .out(multiplexer_2_out), .sel(zy));
  assign not_1_out = ~multiplexer_1_out;  // NOT_Gate not_1, 16 bits wide
  assign not_2_out = ~multiplexer_2_out;  // NOT_Gate not_2, 16 bits wide
  Multiplexer #(.width(16)) multiplexer_3 (.in0(multiplexer_1_out), .in1(not_1_out), .out(multiplexer_3_out), .sel(nx));
  Multiplexer #(.width(16)) multiplexer_4 (.in0(multiplexer_2_out), .in1(not_2_out), .out(multiplexer_4_out), .sel(ny));
  assign not_3_out = ~multiplexer_6_out;  // NOT_Gate not_3, 16 bits wide
  Multiplexer #(.width(16)) multiplexer_5 (.in0(multiplexer_6_out), .in1(not_3_out), .out({ng, out_9[14:0]}), .sel(no));
  assign and_1_out = multiplexer_3_out & multiplexer_4_out;  // AND_Gate and_1, 16 bits wide
  // Add16 add16_1: pin names not known; wires that end beside it: multiplexer_3_out, add16_1_p2, multiplexer_4_out
  Multiplexer #(.width(16)) multiplexer_6 (.in0(and_1_out), .in1(add16_1_p2), .out(multiplexer_6_out), .sel(f));
  or or_1 (or_1_out, out_9[0], out_9[1], out_9[2], out_9[3], out_9[4], out_9[5], out_9[6], out_9[7], out_9[8], out_9[9], out_9[10], out_9[11], out_9[12], out_9[13], out_9[14], ng);
  not not_4 (zr, or_1_out);

  assign out_9[15] = ng;
endmodule
